# Fritzing sketch 01-pwmLED (saved by Fritzing 0.9.3b)
breadboards: 1

parts:
  Part1 = Arduino Micro (Rev3)
  LED1 = LED - 5mm [color="Blue (470nm)" package="5 mm [THT]"]
  R1 = Resistor [tolerance=±5% resistance=220 package=THT]
  LED2 = LED - 5mm [color="Red (633nm)" package="5 mm [THT]"]  # not connected

nets:
  N1: Part1.GND, R1.Pin_1
  N2: Part1.D12_PWM/A11, LED1.anode
  N3: LED1.cathode, R1.Pin_0

// code stored in the sketch: 01-pwmLED.ino

