# Fritzing sketch 02-buttonInput (saved by Fritzing 0.9.3b)
breadboards: 1

parts:
  Part1 = Arduino Micro (Rev3)
  LED1 = LED - 5mm [color="Blue (470nm)" package="5 mm [THT]"]
  R1 = Resistor [tolerance=±5% resistance=220 package=THT]
  S1 = Pushbutton [package="[THT]"]
  R2 = Resistor [tolerance=±5% resistance=220 package=THT]

nets:
  N1: Part1.D7, S1.Pin_3, S1.Pin_4, R2.Pin_0
  N2: Part1.D11_PWM, LED1.anode
  N3: Part1.GND, R1.Pin_1, S1.Pin_1, S1.Pin_2
  N4: Part1.5V, R2.Pin_1
  N5: LED1.cathode, R1.Pin_0

// code stored in the sketch: 01-pwmLED.ino

