# Fritzing sketch 04-photosensor (saved by Fritzing 0.9.3b)
breadboards: 1

parts:
  Part1 = Arduino Micro (Rev3)
  R1 = Resistor [tolerance=±5% resistance=220 package=THT]
  R2 = Photocell (LDR) [package=THT]
  J1 = Piezo Speaker

nets:
  N1: Part1.D11_PWM, J1.pin2
  N2: Part1.GND, R1.Pin_0, J1.pin1
  N3: Part1.5V, R2.pin_1
  N4: Part1.A1, R1.Pin_1, R2.pin_0

// code stored in the sketch: 01-pwmLED.ino

